// Logisim project Group2.circ as structural Verilog
module project_ao (
  input  [15:0] A,
  input  [15:0] B,
  input  [3:0] selector,
  output [15:0] result
);

  wire [15:0] adder_1_out, and_1_out, divider_1_out, divider_1_rem, multiplier_1_out, negator_1_out,
       negator_2_out, or_1_out, shifter_1_out, shifter_2_out, shifter_3_out, shifter_4_out, subtractor_1_out,
       xor_1_out;

  Adder #(.width(16)) adder_1 (.a(A), .b(B), .out(adder_1_out));  // open: cin, cout
  assign and_1_out = A & B;  // AND_Gate and_1, 16 bits wide
  assign or_1_out = A | B;  // OR_Gate or_1, 16 bits wide
  assign xor_1_out = A ^ B;  // XOR_Gate xor_1, 16 bits wide
  Divider #(.width(16)) divider_1 (.a(A), .b(B), .out(divider_1_out), .rem(divider_1_rem));  // open: upper
  Multiplier #(.width(16)) multiplier_1 (.a(A), .b(B), .out(multiplier_1_out));  // open: cin, cout
  Subtractor #(.width(16)) subtractor_1 (.a(A), .b(B), .out(subtractor_1_out));  // open: bin, bout
  Shifter #(.width(16)) shifter_1 (.in(A), .\dist (4'b0010), .out(shifter_1_out));
  Shifter #(.width(16)) shifter_2 (.in(B), .\dist (4'b0010), .out(shifter_2_out));
  Shifter #(.shift("lr"), .width(16)) shifter_3 (.in(A), .\dist (4'b0010), .out(shifter_3_out));
  Shifter #(.shift("lr"), .width(16)) shifter_4 (.in(B), .\dist (4'b0010), .out(shifter_4_out));
  Negator #(.width(16)) negator_1 (.in(A), .out(negator_1_out));
  Negator #(.width(16)) negator_2 (.in(B), .out(negator_2_out));
  Multiplexer #(.select(4), .width(16)) multiplexer_1 (
    .in0(adder_1_out), .in1(and_1_out), .in2(or_1_out), .in3(xor_1_out), .in4(divider_1_out),
    .in5(divider_1_rem), .in6(multiplier_1_out), .in7(subtractor_1_out), .in8(shifter_1_out),
    .in9(shifter_2_out), .in10(shifter_3_out), .in11(shifter_4_out), .in12(negator_1_out),
    .in13(negator_2_out), .out(result), .sel(selector));  // open: in14, in15
endmodule

module project_ro (
  input  [15:0] A,
  input  [15:0] B,
  input  [2:0] selector,
  output result
);

  wire comparator_1_eq, comparator_1_gt, comparator_1_lt, not_1_out, or_1_out, or_2_out;

  Comparator #(.mode("unsigned"), .width(16)) comparator_1 (
    .a(A), .b(B), .gt(comparator_1_gt), .eq(comparator_1_eq), .lt(comparator_1_lt));
  or or_1 (or_1_out, comparator_1_lt, comparator_1_eq);
  or or_2 (or_2_out, comparator_1_gt, comparator_1_eq);
  not not_1 (not_1_out, comparator_1_eq);
  Multiplexer #(.select(3)) multiplexer_1 (
    .in0(comparator_1_gt), .in1(comparator_1_eq), .in2(or_2_out), .in3(comparator_1_lt), .in4(or_1_out),
    .in5(not_1_out), .out(result), .sel(selector));  // open: in6, in7
endmodule

module project_alu (
  input  OE,
  input  [15:0] A,
  input  [15:0] B,
  input  [3:0] selector1,
  input  [2:0] selector2,
  output [15:0] AUDout,
  output [15:0] AUResult,
  output RUResult
);

  project_ao project_ao_1 (.A(A), .B(B), .selector(selector1), .result(AUResult));
  project_ro project_ro_1 (.A(A), .B(B), .selector(selector2), .result(RUResult));
  assign AUDout = OE ? AUResult : 16'bz;  // Controlled_Buffer controlled_buffer_1
endmodule

module Datapath (
  input  [15:0] testing_data,
  input  test_oe,
  input  WE_IR,
  input  OE_IR,
  input  internal_oe,
  input  WE_A,
  input  OE_ALU,
  input  [3:0] AU_selector,
  input  [2:0] LU_selector,
  input  WE_OR,
  input  WE_B,
  input  OE_OR,
  output [7:0] result_MAR,
  output [15:0] IR_constant,
  output [15:0] regA,
  output [15:0] result_MBR,
  output [15:0] ALU_result,
  output [15:0] regB,
  output [15:0] result_OR
);

  wire clock_1_out, undriven;
  wire [7:0] bitselector_1_out, MAR_dout;
  wire [15:0] ALU_audout, instruction_register_dout;

  Clock clock_1 (.out(clock_1_out));
  register16bit instruction_register (
    .in_1(ALU_audout), .WE(WE_IR), .clk(clock_1_out), .OE(OE_IR), .Result(IR_constant),
    .Dout(instruction_register_dout));  // open: reset, Eight_LSBs, Eight_MSBs
  register16bit registerA (
    .in_1(ALU_audout), .WE(WE_A), .clk(clock_1_out), .Result(regA));  // open: reset, OE, Dout, Eight_LSBs, Eight_MSBs
  project_alu ALU (
    .OE(OE_ALU), .A(regA), .B(regB), .selector1(AU_selector), .selector2(LU_selector), .AUDout(ALU_audout),
    .AUResult(ALU_result));  // open: RUResult
  register16bit registerB (
    .in_1(ALU_audout), .WE(WE_B), .clk(clock_1_out), .Result(regB));  // open: reset, OE, Dout, Eight_LSBs, Eight_MSBs
  BitSelector #(.group(8), .width(16)) bitselector_1 (
    .in(instruction_register_dout), .out(bitselector_1_out), .sel(1'b0));
  LED led_1 (.in(ALU_audout[0]));
  LED led_2 (.in(ALU_audout[1]));
  LED led_3 (.in(ALU_audout[2]));
  LED led_4 (.in(ALU_audout[3]));
  LED led_5 (.in(ALU_audout[4]));
  assign ALU_audout = test_oe ? testing_data : 16'bz;  // Controlled_Buffer controlled_buffer_1
  LED led_6 (.in(ALU_audout[5]));
  LED led_7 (.in(ALU_audout[6]));
  LED led_8 (.in(ALU_audout[7]));
  LED led_9 (.in(ALU_audout[8]));
  LED led_10 (.in(ALU_audout[9]));
  LED led_11 (.in(ALU_audout[10]));
  LED led_12 (.in(ALU_audout[11]));
  LED led_13 (.in(ALU_audout[12]));
  LED led_14 (.in(ALU_audout[13]));
  LED led_15 (.in(ALU_audout[14]));
  LED led_16 (.in(ALU_audout[15]));
  assign ALU_audout = internal_oe ? result_MBR : 16'bz;  // Controlled_Buffer controlled_buffer_2
  register8bit MAR (
    .in_1(bitselector_1_out), .clk(clock_1_out), .Result(result_MAR), .Dout(MAR_dout));  // open: WE, reset, OE, Four_LSBs, Four_MSBs
  register16bit output_register (
    .in_1(ALU_audout), .WE(WE_OR), .clk(clock_1_out), .OE(OE_OR), .Result(result_OR), .Dout(ALU_audout));  // open: reset, Eight_LSBs, Eight_MSBs
  register16bit MBR (
    .in_1(ALU_audout), .clk(clock_1_out), .OE(undriven), .Result(result_MBR), .Dout(ALU_audout));  // open: WE, reset, Eight_LSBs, Eight_MSBs
  LED led_17 (.in(ALU_audout[15]));
  LED led_18 (.in(ALU_audout[14]));
  LED led_19 (.in(ALU_audout[13]));
  LED led_20 (.in(ALU_audout[12]));
  LED led_21 (.in(ALU_audout[11]));
  LED led_22 (.in(ALU_audout[10]));
  LED led_23 (.in(ALU_audout[9]));
  LED led_24 (.in(ALU_audout[8]));
  LED led_25 (.in(ALU_audout[7]));
  LED led_26 (.in(ALU_audout[6]));
  LED led_27 (.in(ALU_audout[5]));
  LED led_28 (.in(ALU_audout[4]));
  LED led_29 (.in(ALU_audout[3]));
  LED led_30 (.in(ALU_audout[2]));
  LED led_31 (.in(ALU_audout[1]));
  LED led_32 (.in(ALU_audout[0]));

  // Notes on the sheet:
  //   internal data bus (4bits)
  //   external data bus (4bits)
endmodule

module CPU (
  input  [15:0] testing_data,
  input  test_oe,
  input  in_3,
  input  [7:0] in_4,
  input  [3:0] AU_selector,
  input  [2:0] LU_selector,
  output [7:0] counter_content,
  output [7:0] result_MAR,
  output [15:0] IR_constant,
  output [15:0] regA,
  output [15:0] result_MBR,
  output [15:0] ALU_result,
  output [15:0] regB,
  output [15:0] result_OR,
  output [2:0] out_15
);

  wire clock_1_out, control_unit_1_c0, control_unit_1_c1, control_unit_1_c2, control_unit_1_c3,
       control_unit_1_c4, control_unit_1_c5, control_unit_1_c6, control_unit_1_c7, control_unit_1_c8,
       control_unit_1_c9, control_unit_1_c10, control_unit_1_c11, control_unit_1_c12, control_unit_1_c13,
       control_unit_1_c14, control_unit_1_c15;
  wire [3:0] decimal_decoder_1_dout_2, decimal_decoder_1_dout_3, decimal_decoder_2_dout_2,
       decimal_decoder_3_dout_2, registerA_display_dout_2, registerB_display_dout, registerB_display_dout_2,
       registerB_display_dout_4, registerB_display_dout_5;
  wire [7:0] bitselector_1_out, instruction_register_eight_msbs, MAR_dout;
  wire [15:0] ALU_audout, bit_extender_1_out, bit_extender_2_out, instruction_register_dout,
       Random_Access_Memory_dout;
  wire [23:0] decimal_decoder_1_dout;
  wire [23:8] registerB_display_dout_3;
  wire [27:0] decimal_decoder_2_dout, decimal_decoder_3_dout, registerA_display_dout;

  decimal_decoder registerA_display (.Din(regA), .Dout({registerA_display_dout_2, registerA_display_dout}));
  _7_Segment_Display u_7_segment_display_1 (
    .g(registerA_display_dout[15]), .f(registerA_display_dout[14]), .a(registerA_display_dout[13]),
    .b(registerA_display_dout[12]), .e(registerA_display_dout_2[3]), .d(registerA_display_dout_2[2]),
    .c(registerA_display_dout_2[1]), .dp(registerA_display_dout_2[0]));
  _7_Segment_Display u_7_segment_display_2 (
    .g(registerA_display_dout[11]), .f(registerA_display_dout[10]), .a(registerA_display_dout[9]),
    .b(registerA_display_dout[8]), .e(registerA_display_dout[27]), .d(registerA_display_dout[26]),
    .c(registerA_display_dout[25]), .dp(registerA_display_dout[24]));
  _7_Segment_Display u_7_segment_display_3 (
    .g(registerA_display_dout[7]), .f(registerA_display_dout[6]), .a(registerA_display_dout[5]),
    .b(registerA_display_dout[4]), .e(registerA_display_dout[23]), .d(registerA_display_dout[22]),
    .c(registerA_display_dout[21]), .dp(registerA_display_dout[20]));
  _7_Segment_Display u_7_segment_display_4 (
    .g(registerA_display_dout[3]), .f(registerA_display_dout[2]), .a(registerA_display_dout[1]),
    .b(registerA_display_dout[0]), .e(registerA_display_dout[19]), .d(registerA_display_dout[18]),
    .c(registerA_display_dout[17]), .dp(registerA_display_dout[16]));
  Clock clock_1 (.out(clock_1_out));
  _7_Segment_Display u_7_segment_display_5 (
    .g(registerB_display_dout_3[15]), .f(registerB_display_dout_3[14]), .a(registerB_display_dout_3[13]),
    .b(registerB_display_dout_3[12]), .e(registerB_display_dout_5[3]), .d(registerB_display_dout_5[2]),
    .c(registerB_display_dout_5[1]), .dp(registerB_display_dout_5[0]));
  _7_Segment_Display u_7_segment_display_6 (
    .g(registerB_display_dout_3[11]), .f(registerB_display_dout_3[10]), .a(registerB_display_dout_3[9]),
    .b(registerB_display_dout_3[8]), .e(registerB_display_dout_4[3]), .d(registerB_display_dout_4[2]),
    .c(registerB_display_dout_4[1]), .dp(registerB_display_dout_4[0]));
  register16bit instruction_register (
    .in_1(ALU_audout), .WE(control_unit_1_c7), .clk(clock_1_out), .OE(control_unit_1_c8),
    .Result(IR_constant), .Dout(instruction_register_dout), .Eight_MSBs(instruction_register_eight_msbs));  // open: reset, Eight_LSBs
  register16bit registerA (
    .in_1(ALU_audout), .WE(control_unit_1_c12), .clk(clock_1_out), .Result(regA));  // open: reset, OE, Dout, Eight_LSBs, Eight_MSBs
  project_alu ALU (
    .OE(control_unit_1_c11), .A(regA), .B(regB), .selector1(AU_selector), .selector2(LU_selector),
    .AUDout(ALU_audout), .AUResult(ALU_result));  // open: RUResult
  register16bit registerB (
    .in_1(ALU_audout), .WE(control_unit_1_c13), .clk(clock_1_out), .Result(regB));  // open: reset, OE, Dout, Eight_LSBs, Eight_MSBs
  decimal_decoder registerB_display (
    .Din(regB),
    .Dout({registerB_display_dout_5, registerB_display_dout_4, registerB_display_dout_3, registerB_display_dout_2, registerB_display_dout}));
  _7_Segment_Display u_7_segment_display_7 (
    .g(registerB_display_dout[3]), .f(registerB_display_dout[2]), .a(registerB_display_dout[1]),
    .b(registerB_display_dout[0]), .e(registerB_display_dout_3[19]), .d(registerB_display_dout_3[18]),
    .c(registerB_display_dout_3[17]), .dp(registerB_display_dout_3[16]));
  _7_Segment_Display u_7_segment_display_8 (
    .g(registerB_display_dout_2[3]), .f(registerB_display_dout_2[2]), .a(registerB_display_dout_2[1]),
    .b(registerB_display_dout_2[0]), .e(registerB_display_dout_3[23]), .d(registerB_display_dout_3[22]),
    .c(registerB_display_dout_3[21]), .dp(registerB_display_dout_3[20]));
  BitSelector #(.group(8), .width(16)) bitselector_1 (
    .in(instruction_register_dout), .out(bitselector_1_out), .sel(1'b0));
  LED led_1 (.in(ALU_audout[0]));
  LED led_2 (.in(ALU_audout[1]));
  LED led_3 (.in(ALU_audout[2]));
  LED led_4 (.in(ALU_audout[3]));
  LED led_5 (.in(ALU_audout[4]));
  assign ALU_audout = test_oe ? testing_data : 16'bz;  // Controlled_Buffer controlled_buffer_1
  LED led_6 (.in(ALU_audout[5]));
  LED led_7 (.in(ALU_audout[6]));
  LED led_8 (.in(ALU_audout[7]));
  LED led_9 (.in(ALU_audout[8]));
  LED led_10 (.in(ALU_audout[9]));
  LED led_11 (.in(ALU_audout[10]));
  LED led_12 (.in(ALU_audout[11]));
  LED led_13 (.in(ALU_audout[12]));
  LED led_14 (.in(ALU_audout[13]));
  LED led_15 (.in(ALU_audout[14]));
  LED led_16 (.in(ALU_audout[15]));
  assign bitselector_1_out = control_unit_1_c0 ? counter_content : 8'bz;  // Controlled_Buffer controlled_buffer_2
  assign ALU_audout = control_unit_1_c5 ? result_MBR : 16'bz;  // Controlled_Buffer controlled_buffer_3
  register8bit MAR (
    .in_1(bitselector_1_out), .WE(control_unit_1_c9), .clk(clock_1_out), .OE(control_unit_1_c10),
    .Result(result_MAR), .Dout(MAR_dout));  // open: reset, Four_LSBs, Four_MSBs
  register16bit output_register (
    .in_1(ALU_audout), .WE(control_unit_1_c15), .clk(clock_1_out), .OE(control_unit_1_c14),
    .Result(result_OR), .Dout(ALU_audout));  // open: reset, Eight_LSBs, Eight_MSBs
  _7_Segment_Display u_7_segment_display_9 (
    .g(decimal_decoder_1_dout[15]), .f(decimal_decoder_1_dout[14]), .a(decimal_decoder_1_dout[13]),
    .b(decimal_decoder_1_dout[12]), .e(decimal_decoder_1_dout_3[3]), .d(decimal_decoder_1_dout_3[2]),
    .c(decimal_decoder_1_dout_3[1]), .dp(decimal_decoder_1_dout_3[0]));
  _7_Segment_Display u_7_segment_display_10 (
    .g(decimal_decoder_1_dout[11]), .f(decimal_decoder_1_dout[10]), .a(decimal_decoder_1_dout[9]),
    .b(decimal_decoder_1_dout[8]), .e(decimal_decoder_1_dout_2[3]), .d(decimal_decoder_1_dout_2[2]),
    .c(decimal_decoder_1_dout_2[1]), .dp(decimal_decoder_1_dout_2[0]));
  Counter #(.max('h3)) Program_Counter (
    .count(control_unit_1_c1), .clk(clock_1_out), .D(bitselector_1_out), .Q(counter_content));  // open: clr, load, up, carry
  register16bit MBR (
    .in_1(ALU_audout), .WE(control_unit_1_c4), .clk(clock_1_out), .OE(control_unit_1_c6),
    .Result(result_MBR), .Dout(ALU_audout));  // open: reset, Eight_LSBs, Eight_MSBs
  decimal_decoder decimal_decoder_1 (
    .Din(result_OR), .Dout({decimal_decoder_1_dout_3, decimal_decoder_1_dout_2, decimal_decoder_1_dout}));
  _7_Segment_Display u_7_segment_display_11 (
    .g(decimal_decoder_1_dout[7]), .f(decimal_decoder_1_dout[6]), .a(decimal_decoder_1_dout[5]),
    .b(decimal_decoder_1_dout[4]), .e(decimal_decoder_1_dout[23]), .d(decimal_decoder_1_dout[22]),
    .c(decimal_decoder_1_dout[21]), .dp(decimal_decoder_1_dout[20]));
  _7_Segment_Display u_7_segment_display_12 (
    .g(decimal_decoder_1_dout[3]), .f(decimal_decoder_1_dout[2]), .a(decimal_decoder_1_dout[1]),
    .b(decimal_decoder_1_dout[0]), .e(decimal_decoder_1_dout[19]), .d(decimal_decoder_1_dout[18]),
    .c(decimal_decoder_1_dout[17]), .dp(decimal_decoder_1_dout[16]));
  LED led_17 (.in(ALU_audout[15]));
  LED led_18 (.in(ALU_audout[14]));
  Counter #(.max('h5), .width(3)) counter_1 (.clk(clock_1_out), .Q(out_15));  // open: clr, load, up, count, D, carry
  assign bit_extender_1_out = {{8{counter_content[7]}}, counter_content};  // Bit_Extender bit_extender_1
  LED led_19 (.in(ALU_audout[13]));
  LED led_20 (.in(ALU_audout[12]));
  LED led_21 (.in(ALU_audout[11]));
  LED led_22 (.in(ALU_audout[10]));
  LED led_23 (.in(ALU_audout[9]));
  LED led_24 (.in(ALU_audout[8]));
  LED led_25 (.in(ALU_audout[7]));
  LED led_26 (.in(ALU_audout[6]));
  assign bit_extender_2_out = {{13{1'b0}}, out_15};  // Bit_Extender bit_extender_2
  _7_Segment_Display u_7_segment_display_13 (
    .g(decimal_decoder_3_dout[15]), .f(decimal_decoder_3_dout[14]), .a(decimal_decoder_3_dout[13]),
    .b(decimal_decoder_3_dout[12]), .e(decimal_decoder_3_dout_2[3]), .d(decimal_decoder_3_dout_2[2]),
    .c(decimal_decoder_3_dout_2[1]), .dp(decimal_decoder_3_dout_2[0]));
  LED led_27 (.in(ALU_audout[5]));
  LED led_28 (.in(ALU_audout[4]));
  LED led_29 (.in(ALU_audout[3]));
  decimal_decoder decimal_decoder_2 (
    .Din(bit_extender_2_out), .Dout({decimal_decoder_2_dout_2, decimal_decoder_2_dout}));
  _7_Segment_Display u_7_segment_display_14 (
    .g(decimal_decoder_2_dout[15]), .f(decimal_decoder_2_dout[14]), .a(decimal_decoder_2_dout[13]),
    .b(decimal_decoder_2_dout[12]), .e(decimal_decoder_2_dout_2[3]), .d(decimal_decoder_2_dout_2[2]),
    .c(decimal_decoder_2_dout_2[1]), .dp(decimal_decoder_2_dout_2[0]));
  _7_Segment_Display u_7_segment_display_15 (
    .g(decimal_decoder_2_dout[11]), .f(decimal_decoder_2_dout[10]), .a(decimal_decoder_2_dout[9]),
    .b(decimal_decoder_2_dout[8]), .e(decimal_decoder_2_dout[27]), .d(decimal_decoder_2_dout[26]),
    .c(decimal_decoder_2_dout[25]), .dp(decimal_decoder_2_dout[24]));
  decimal_decoder decimal_decoder_3 (
    .Din(bit_extender_1_out), .Dout({decimal_decoder_3_dout_2, decimal_decoder_3_dout}));
  _7_Segment_Display u_7_segment_display_16 (
    .g(decimal_decoder_3_dout[11]), .f(decimal_decoder_3_dout[10]), .a(decimal_decoder_3_dout[9]),
    .b(decimal_decoder_3_dout[8]), .e(decimal_decoder_3_dout[27]), .d(decimal_decoder_3_dout[26]),
    .c(decimal_decoder_3_dout[25]), .dp(decimal_decoder_3_dout[24]));
  _7_Segment_Display u_7_segment_display_17 (
    .g(decimal_decoder_3_dout[7]), .f(decimal_decoder_3_dout[6]), .a(decimal_decoder_3_dout[5]),
    .b(decimal_decoder_3_dout[4]), .e(decimal_decoder_3_dout[23]), .d(decimal_decoder_3_dout[22]),
    .c(decimal_decoder_3_dout[21]), .dp(decimal_decoder_3_dout[20]));
  LED led_30 (.in(ALU_audout[2]));
  LED led_31 (.in(ALU_audout[1]));
  _7_Segment_Display u_7_segment_display_18 (
    .g(decimal_decoder_2_dout[7]), .f(decimal_decoder_2_dout[6]), .a(decimal_decoder_2_dout[5]),
    .b(decimal_decoder_2_dout[4]), .e(decimal_decoder_2_dout[23]), .d(decimal_decoder_2_dout[22]),
    .c(decimal_decoder_2_dout[21]), .dp(decimal_decoder_2_dout[20]));
  _7_Segment_Display u_7_segment_display_19 (
    .g(decimal_decoder_2_dout[3]), .f(decimal_decoder_2_dout[2]), .a(decimal_decoder_2_dout[1]),
    .b(decimal_decoder_2_dout[0]), .e(decimal_decoder_2_dout[19]), .d(decimal_decoder_2_dout[18]),
    .c(decimal_decoder_2_dout[17]), .dp(decimal_decoder_2_dout[16]));
  _7_Segment_Display u_7_segment_display_20 (
    .g(decimal_decoder_3_dout[3]), .f(decimal_decoder_3_dout[2]), .a(decimal_decoder_3_dout[1]),
    .b(decimal_decoder_3_dout[0]), .e(decimal_decoder_3_dout[19]), .d(decimal_decoder_3_dout[18]),
    .c(decimal_decoder_3_dout[17]), .dp(decimal_decoder_3_dout[16]));
  LED led_32 (.in(ALU_audout[0]));
  assign MAR_dout = in_3 ? in_4 : 8'bz;  // Controlled_Buffer controlled_buffer_4
  control_unit control_unit_1 (
    .OPC7(instruction_register_eight_msbs[0]), .OPC6(instruction_register_eight_msbs[1]),
    .OPC5(instruction_register_eight_msbs[2]), .OPC4(instruction_register_eight_msbs[3]),
    .OPC3(instruction_register_eight_msbs[4]), .OPC2(instruction_register_eight_msbs[5]),
    .OPC1(instruction_register_eight_msbs[6]), .OP0(instruction_register_eight_msbs[7]), .SC2(out_15[0]),
    .SC1(out_15[1]), .SC0(out_15[2]), .C0(control_unit_1_c0), .C1(control_unit_1_c1), .C2(control_unit_1_c2),
    .C3(control_unit_1_c3), .C4(control_unit_1_c4), .C5(control_unit_1_c5), .C6(control_unit_1_c6),
    .C7(control_unit_1_c7), .C8(control_unit_1_c8), .C9(control_unit_1_c9), .C10(control_unit_1_c10),
    .C11(control_unit_1_c11), .C12(control_unit_1_c12), .C13(control_unit_1_c13), .C14(control_unit_1_c14),
    .C15(control_unit_1_c15));
  RAM #(.dataWidth(16), .enables("line")) Random_Access_Memory (
    .addr(MAR_dout), .we(control_unit_1_c2), .clk(clock_1_out), .din(ALU_audout),
    .dout(Random_Access_Memory_dout));
  assign ALU_audout = control_unit_1_c3 ? Random_Access_Memory_dout : 16'bz;  // Controlled_Buffer controlled_buffer_5

  // Notes on the sheet:
  //   internal data bus (8bits)
  //   external data bus (4bits)
  //   Random Access Memory
endmodule

module register16bit (
  input  [15:0] in_1,
  input  WE,
  input  clk,
  input  reset,
  input  OE,
  output [15:0] Result,
  output [15:0] Dout,
  output [7:0] Eight_LSBs,
  output [7:0] Eight_MSBs
);

  Register #(.width(16)) register_1 (.D(in_1), .en(WE), .clk(clk), .Q(Result), .clr(reset));
  assign Dout = OE ? Result : 16'bz;  // Controlled_Buffer controlled_buffer_1
  BitSelector #(.group(8), .width(16)) bitselector_1 (.in(Dout), .out(Eight_LSBs), .sel(1'b0));
  BitSelector #(.group(8), .width(16)) bitselector_2 (.in(Dout), .out(Eight_MSBs), .sel(1'b1));
endmodule

module decimal_decoder (
  input  [15:0] Din,
  output [31:0] Dout
);

  ROM #(.addrWidth(16), .dataWidth(32)) rom_1 (
    .addr(Din),
    .data({Dout[31:28], Dout[15:12], Dout[27:24], Dout[11:8], Dout[23:20], Dout[7:4], Dout[19:16], Dout[3:0]}));

  // Notes on the sheet:
  //   contents of rom_1 (hex, n*v repeats v):
  //   e7 21 cb 6b 2d 6e ee 23 ef 2f 21e7 2121 21cb 216b 212d 216e 21ee 2123 21ef 212f cbe7 cb21 cbcb cb6b
  //   cb2d cb6e cbee cb23 cbef cb2f 6be7 6b21 6bcb 6b6b 6b2d 6b6e 6bee 6b23 6bef 6b2f 2de7 2d21 2dcb 2d6b
  //   2d2d 2d6e 2dee 2d23 2def 2d2f 6ee7 6e21 6ecb 6e6b 6e2d 6e6e 6eee 6e23 6eef 6e2f eee7 ee21 eecb ee6b
  //   ee2d ee6e eeee ee23 eeef ee2f 23e7 2321 23cb 236b 232d 236e 23ee 2323 23ef 232f efe7 ef21 efcb ef6b
  //   ef2d ef6e efee ef23 efef ef2f 2fe7 2f21 2fcb 2f6b 2f2d 2f6e 2fee 2f23 2fef 2f2f 21e7e7 21e721 21e7cb
  //   21e76b 21e72d 21e76e 21e7ee 21e723 21e7ef 21e72f 2121e7 212121 2121cb 21216b 21212d 21216e 2121ee
  //   212123 2121ef 21212f 21cbe7 21cb21 21cbcb 21cb6b 21cb2d 21cb6e 21cbee 21cb23 21cbef 21cb2f 216be7
  //   216b21 216bcb 216b6b 216b2d 216b6e 216bee 216b23 216bef 216b2f 212de7 212d21 212dcb 212d6b 212d2d
  //   212d6e 212dee 212d23 212def 212d2f 216ee7 216e21 216ecb 216e6b 216e2d 216e6e 216eee 216e23 216eef
  //   216e2f 21eee7 21ee21 21eecb 21ee6b 21ee2d 21ee6e 21eeee 21ee23 21eeef 21ee2f 2123e7 212321 2123cb
  //   21236b 21232d 21236e 2123ee 212323 2123ef 21232f 21efe7 21ef21 21efcb 21ef6b 21ef2d 21ef6e 21efee
  //   21ef23 21efef 21ef2f 212fe7 212f21 212fcb 212f6b 212f2d 212f6e 212fee 212f23 212fef 212f2f cbe7e7
  //   cbe721 cbe7cb cbe76b cbe72d cbe76e cbe7ee cbe723 cbe7ef cbe72f cb21e7 cb2121 cb21cb cb216b cb212d
  //   cb216e cb21ee cb2123 cb21ef cb212f cbcbe7 cbcb21 cbcbcb cbcb6b cbcb2d cbcb6e cbcbee cbcb23 cbcbef
  //   cbcb2f cb6be7 cb6b21 cb6bcb cb6b6b cb6b2d cb6b6e cb6bee cb6b23 cb6bef cb6b2f cb2de7 cb2d21 cb2dcb
  //   cb2d6b cb2d2d cb2d6e cb2dee cb2d23 cb2def cb2d2f cb6ee7 cb6e21 cb6ecb cb6e6b cb6e2d cb6e6e
endmodule

module control_unit (
  input  OPC7,
  input  OPC6,
  input  OPC5,
  input  OPC4,
  input  OPC3,
  input  OPC2,
  input  OPC1,
  input  OP0,
  input  SC2,
  input  SC1,
  input  SC0,
  output C0,
  output C1,
  output C2,
  output C3,
  output C4,
  output C5,
  output C6,
  output C7,
  output C8,
  output C9,
  output C10,
  output C11,
  output C12,
  output C13,
  output C14,
  output C15
);

  wire and_4_out, and_5_out, and_6_out, and_7_out, and_8_out, and_9_out, and_10_out, and_13_out, and_14_out,
       and_15_out, and_16_out, and_17_out, and_18_out, and_19_out, and_20_out, not_1_out, not_2_out,
       not_3_out, not_4_out, not_5_out;

  not not_1 (not_1_out, OPC1);
  not not_2 (not_2_out, OP0);
  not not_3 (not_3_out, SC2);
  not not_4 (not_4_out, SC1);
  not not_5 (not_5_out, SC0);
  and and_1 (C0, not_3_out, not_4_out, not_5_out);
  and and_2 (C1, not_3_out, not_4_out, SC0);
  and and_3 (C2, OPC1, OP0, SC2, not_4_out, not_5_out);
  and and_4 (and_4_out, not_3_out, not_4_out, SC0);
  and and_5 (and_5_out, not_1_out, SC2, not_4_out, not_5_out);
  and and_6 (and_6_out, not_3_out, not_4_out, SC0);
  and and_7 (and_7_out, not_1_out, SC2, not_4_out, not_5_out);
  and and_8 (and_8_out, OPC1, OP0, not_3_out, SC0);
  and and_9 (and_9_out, not_3_out, SC1, not_5_out);
  and and_10 (and_10_out, not_1_out, SC2, not_4_out, SC0);
  and and_11 (C6, OPC1, OP0, SC2, not_4_out, not_5_out);
  and and_12 (C7, not_3_out, SC1, not_5_out);
  and and_13 (and_13_out, not_1_out, not_3_out, SC1, SC0);
  and and_14 (and_14_out, OP0, not_3_out, SC1, SC0);
  and and_15 (and_15_out, not_3_out, not_4_out, not_5_out);
  and and_16 (and_16_out, not_1_out, not_3_out, SC1, SC0);
  and and_17 (and_17_out, OP0, not_3_out, SC1, SC0);
  and and_18 (and_18_out, not_3_out, not_4_out, SC0);
  and and_19 (and_19_out, not_1_out, SC2, not_4_out, not_5_out);
  and and_20 (and_20_out, OP0, SC2, not_4_out, not_5_out);
  and and_21 (C11, OPC1, not_2_out, not_3_out, SC1, SC0);
  and and_22 (C12, not_1_out, not_2_out, SC2, not_4_out, SC0);
  and and_23 (C13, not_1_out, OP0, SC2, not_4_out, SC0);
  and and_24 (C14, OPC1, OP0, not_3_out, SC1, SC0);
  and and_25 (C15, OPC1, not_2_out, not_3_out, SC1, SC0);
  or or_1 (C3, and_4_out, and_5_out);
  or or_2 (C4, and_6_out, and_7_out, and_8_out);
  or or_3 (C5, and_9_out, and_10_out);
  or or_4 (C8, and_13_out, and_14_out);
  or or_5 (C9, and_15_out, and_16_out, and_17_out);
  or or_6 (C10, and_18_out, and_19_out, and_20_out);
endmodule

module register8bit (
  input  [7:0] in_1,
  input  WE,
  input  clk,
  input  reset,
  input  OE,
  output [7:0] Result,
  output [7:0] Dout,
  output [3:0] Four_LSBs,
  output [3:0] Four_MSBs
);

  Register register_1 (.D(in_1), .en(WE), .clk(clk), .Q(Result), .clr(reset));
  assign Dout = OE ? Result : 8'bz;  // Controlled_Buffer controlled_buffer_1
  BitSelector #(.group(4)) bitselector_1 (.in(Dout), .out(Four_LSBs), .sel(1'b0));
  BitSelector #(.group(4)) bitselector_2 (.in(Dout), .out(Four_MSBs), .sel(1'b1));
endmodule

module CPU_possible (
  input  [15:0] in_1,
  input  in_2,
  input  in_3,
  input  in_4,
  input  in_5,
  input  in_6,
  input  in_7,
  input  [3:0] AU_sel,
  input  [2:0] LU_sel,
  input  in_10,
  input  in_11,
  input  in_12
);

  Datapath datapath_1 (
    .testing_data(in_1), .test_oe(in_2), .WE_IR(in_3), .OE_IR(in_4), .internal_oe(in_5), .WE_A(in_6),
    .OE_ALU(in_7), .AU_selector(AU_sel), .LU_selector(LU_sel), .WE_OR(in_10), .WE_B(in_11), .OE_OR(in_12));  // open: result_MAR, IR_constant, regA, result_MBR, ALU_result, regB, result_OR
endmodule
